// Logisim project 8 bit data path.circ as structural Verilog: 4 circuits, main circuit main
module main (
  input  in_1,
  output [7:0] out_2,
  output out_3,
  output [7:0] out_4,
  output [7:0] out_5,
  output [12:0] out_6
);

  wire clock_1_out;
  wire [3:0] adder_1_out, register_1_q;

  Register #(.width(4)) register_1 (.D(adder_1_out), .Q(register_1_q), .clk(clock_1_out));  // open: en, clr
  Adder #(.width(4)) adder_1 (.a(register_1_q), .b(4'b0001), .out(adder_1_out));  // open: cin, cout
  ROM #(.addrWidth(4), .dataWidth(13)) rom_1 (.addr(register_1_q), .data(out_6));  // open: sel
  Clock clock_1 (.out(clock_1_out));
  _8_bit_register u_8_bit_register_1 (
    .Write_data(out_2), .Read_Data_1(out_4), .Read_Register_1(out_6[8:6]), .Read_Data_2(out_5),
    .Read_Register_2(out_6[5:3]), .Write_Register(out_6[2:0]), .Write_Enable_Key(out_6[12]),
    .Clock(clock_1_out));
  _8_Bit_ALU u_8_bit_alu_1 (.in_1(in_1), .in_2(out_4), .in_3(out_5), .in_4(out_6[11:9]), .out_5(out_2), .Cout(out_3));

  // Notes on the sheet:
  //   contents of rom_1 (hex, n*v repeats v):
  //   210
endmodule

module _8_bit_register (
  input  [2:0] Read_Register_1,
  input  [7:0] Write_data,
  input  [2:0] Write_Register,
  input  [2:0] Read_Register_2,
  input  Write_Enable_Key,
  input  Clock,
  output [7:0] Read_Data_1,
  output [7:0] Read_Data_2
);

  wire and_1_out, decoder_1_out0, decoder_1_out1, decoder_1_out2, decoder_1_out3, decoder_1_out4,
       decoder_1_out5, decoder_1_out6, decoder_1_out7;
  wire [7:0] and_2_out, and_3_out, demultiplexer_1_out0, demultiplexer_1_out1, demultiplexer_1_out2,
       demultiplexer_1_out3, demultiplexer_1_out4, demultiplexer_1_out5, demultiplexer_1_out6,
       demultiplexer_1_out7, register_1_q, register_2_q, register_3_q, register_4_q, register_5_q,
       register_6_q, register_7_q, register_8_q, register_9_q, register_10_q;

  Demultiplexer #(.select(3), .width(8)) demultiplexer_1 (
    .out0(demultiplexer_1_out0), .out1(demultiplexer_1_out1), .out2(demultiplexer_1_out2),
    .out3(demultiplexer_1_out3), .out4(demultiplexer_1_out4), .out5(demultiplexer_1_out5),
    .out6(demultiplexer_1_out6), .out7(demultiplexer_1_out7), .in(Write_data), .sel(Write_Register));  // open: en
  Decoder #(.select(3)) decoder_1 (
    .out0(decoder_1_out0), .out1(decoder_1_out1), .out2(decoder_1_out2), .out3(decoder_1_out3),
    .out4(decoder_1_out4), .out5(decoder_1_out5), .out6(decoder_1_out6), .out7(decoder_1_out7),
    .sel(Write_Register));  // open: en
  and and_1 (and_1_out, Write_Enable_Key, Clock);
  Register register_1 (.D(demultiplexer_1_out0), .en(decoder_1_out0), .Q(register_1_q), .clk(and_1_out));  // open: clr
  Register register_2 (.D(demultiplexer_1_out1), .en(decoder_1_out1), .Q(register_2_q), .clk(and_1_out));  // open: clr
  Register register_3 (.D(demultiplexer_1_out2), .en(decoder_1_out2), .Q(register_3_q), .clk(and_1_out));  // open: clr
  Register register_4 (.D(demultiplexer_1_out3), .en(decoder_1_out3), .Q(register_4_q), .clk(and_1_out));  // open: clr
  Register register_5 (.D(demultiplexer_1_out4), .en(decoder_1_out4), .Q(register_5_q), .clk(and_1_out));  // open: clr
  Register register_6 (.D(demultiplexer_1_out5), .en(decoder_1_out5), .Q(register_6_q), .clk(and_1_out));  // open: clr
  Register register_7 (.D(demultiplexer_1_out6), .en(decoder_1_out6), .Q(register_7_q), .clk(and_1_out));  // open: clr
  Register register_8 (.D(demultiplexer_1_out6), .en(decoder_1_out6), .Q(register_8_q));  // open: clk, clr
  Register register_9 (.D(demultiplexer_1_out7), .en(decoder_1_out7), .Q(register_9_q), .clk(and_1_out));  // open: clr
  Register register_10 (
    .D(demultiplexer_1_out7), .en(decoder_1_out7), .Q(register_10_q), .clk(and_1_out));  // open: clr
  assign and_2_out = register_7_q & register_8_q;  // AND_Gate and_2, 8 bits wide
  assign and_3_out = register_9_q & register_10_q;  // AND_Gate and_3, 8 bits wide
  Multiplexer #(.select(3), .width(8)) multiplexer_1 (
    .in0(register_1_q), .in1(register_2_q), .in2(register_3_q), .in3(register_4_q), .in4(register_5_q),
    .in5(register_6_q), .in6(and_2_out), .in7(and_3_out), .out(Read_Data_1), .sel(Read_Register_1));  // open: en
  Multiplexer #(.select(3), .width(8)) multiplexer_2 (
    .in0(register_1_q), .in1(register_2_q), .in2(register_3_q), .in3(register_4_q), .in4(register_5_q),
    .in5(register_6_q), .in6(and_2_out), .in7(and_3_out), .out(Read_Data_2), .sel(Read_Register_2));  // open: en
endmodule

module _1_Bit_ALU (
  input  Cin,
  input  A,
  input  B,
  input  [2:0] Opcode,
  output Output,
  output Cout
);

  wire and_1_out, and_2_out, and_3_out, and_4_out, and_5_out, and_6_out, and_7_out, not_1_out, not_2_out,
       or_1_out, or_2_out, or_3_out, xor_1_out, xor_2_out;

  xor xor_1 (xor_1_out, A, B);
  not not_1 (not_1_out, A);
  and and_1 (and_1_out, A, B);
  or or_1 (or_1_out, A, B);
  xor xor_2 (xor_2_out, xor_1_out, Cin);
  and and_2 (and_2_out, Cin, xor_1_out);
  and and_3 (and_3_out, A, B);
  not not_2 (not_2_out, xor_1_out);
  and and_4 (and_4_out, not_1_out, B);
  or or_2 (or_2_out, and_2_out, and_3_out);
  and and_5 (and_5_out, not_2_out, Cin);
  or or_3 (or_3_out, and_5_out, and_4_out);
  and and_6 (and_6_out, or_2_out, Opcode[1]);
  Multiplexer multiplexer_1 (.in0(and_6_out), .in1(and_7_out), .out(Cout), .sel(Opcode[0]));  // open: en
  and and_7 (and_7_out, Opcode[1], or_3_out);
  Multiplexer #(.select(3)) multiplexer_2 (
    .in0(and_1_out), .in1(or_1_out), .in2(xor_2_out), .in3(xor_2_out), .in4(xor_1_out), .out(Output),
    .sel(Opcode));  // open: in5, in6, in7, en
endmodule

module _8_Bit_ALU (
  input  in_1,
  input  [7:0] in_2,
  input  [7:0] in_3,
  input  [2:0] in_4,
  output [7:0] out_5,
  output Cout
);

  wire n1_bit_alu_1_cout, n1_bit_alu_2_cout, n1_bit_alu_3_cout, n1_bit_alu_4_cout, n1_bit_alu_5_cout,
       n1_bit_alu_6_cout, n1_bit_alu_7_cout;

  _1_Bit_ALU u_1_bit_alu_1 (
    .Cin(in_1), .A(in_2[0]), .B(in_3[0]), .Output(out_5[0]), .Cout(n1_bit_alu_1_cout), .Opcode(in_4));
  _1_Bit_ALU u_1_bit_alu_2 (
    .Cin(n1_bit_alu_1_cout), .A(in_2[1]), .B(in_3[1]), .Output(out_5[1]), .Cout(n1_bit_alu_2_cout),
    .Opcode(in_4));
  _1_Bit_ALU u_1_bit_alu_3 (
    .Cin(n1_bit_alu_2_cout), .A(in_2[2]), .B(in_3[2]), .Output(out_5[2]), .Cout(n1_bit_alu_3_cout),
    .Opcode(in_4));
  _1_Bit_ALU u_1_bit_alu_4 (
    .Cin(n1_bit_alu_3_cout), .A(in_2[3]), .B(in_3[3]), .Output(out_5[3]), .Cout(n1_bit_alu_4_cout),
    .Opcode(in_4));
  _1_Bit_ALU u_1_bit_alu_5 (
    .Cin(n1_bit_alu_4_cout), .A(in_2[4]), .B(in_3[4]), .Output(out_5[4]), .Cout(n1_bit_alu_5_cout),
    .Opcode(in_4));
  _1_Bit_ALU u_1_bit_alu_6 (
    .Cin(n1_bit_alu_5_cout), .A(in_2[5]), .B(in_3[5]), .Output(out_5[5]), .Cout(n1_bit_alu_6_cout),
    .Opcode(in_4));
  _1_Bit_ALU u_1_bit_alu_7 (
    .Cin(n1_bit_alu_6_cout), .A(in_2[6]), .B(in_3[6]), .Output(out_5[6]), .Cout(n1_bit_alu_7_cout),
    .Opcode(in_4));
  _1_Bit_ALU u_1_bit_alu_8 (
    .Cin(n1_bit_alu_7_cout), .A(in_2[7]), .B(in_3[7]), .Output(out_5[7]), .Cout(Cout), .Opcode(in_4));
endmodule
