// Logisim project Koushik Banerjee_1812171642.circ as structural Verilog: 15 circuits, main circuit main
module main (
);

  NAND nand_1 ();  // open: _3, _1, _2, _4, _5, _9, _8, _10, _12, _11, _13, _6
  _3_input_OR u_3_input_or_1 ();  // open: _1, _2, _8, _3, _4, _5, _11, _12, _13, _9, _6, _10, _7, _14
  NOT not_1 ();  // open: _1, _2, _3, _4, _5, _6, _9, _8, _11, _10, _13, _12
  _3_input_AND u_3_input_and_1 ();  // open: _14, _1, _2, _13, _3, _4, _5, _9, _10, _11, _7, _12, _6, _8
  AND and_1 ();  // open: _1, _2, _4, _9, _10, _12, _13, _3, _6, _11, _5, _8
  XOR_IC xor_ic_1 ();  // open: _1, _2, _4, _5, _10, _9, _13, _12, _3, _6, _8, _11
  _2_input_OR u_2_input_or_1 ();  // open: _1, _2, _4, _5, _9, _10, _12, _13, _3, _6, _8, _11
  _4_1_MUX u_4_1_mux_1 ();  // open: I0, I1, I2, I3, S1, S0, out_7
  _8_1_MUX u_8_1_mux_1 ();  // open: _17, _16, _15, _14, S0, _13, _12, _11, _10, S1, S2, out_12
endmodule

module NAND (
  input  _1,
  input  _2,
  input  _4,
  input  _5,
  input  _9,
  input  _10,
  input  _12,
  input  _13,
  output _3,
  output _6,
  output _8,
  output _11
);

  nand nand_1 (_3, _1, _2);
  nand nand_2 (_6, _4, _5);
  nand nand_3 (_8, _9, _10);
  nand nand_4 (_11, _12, _13);
endmodule

module AND (
  input  _1,
  input  _2,
  input  _4,
  input  _5,
  input  _9,
  input  _10,
  input  _12,
  input  _13,
  output _3,
  output _6,
  output _8,
  output _11
);

  and and_1 (_3, _1, _2);
  and and_2 (_6, _4, _5);
  and and_3 (_8, _9, _10);
  and and_4 (_11, _12, _13);
endmodule

module NOT (
  input  _1,
  input  _3,
  input  _5,
  input  _9,
  input  _11,
  input  _13,
  output _2,
  output _4,
  output _6,
  output _8,
  output _10,
  output _12
);

  not not_1 (_2, _1);
  not not_2 (_4, _3);
  not not_3 (_6, _5);
  not not_4 (_8, _9);
  not not_5 (_10, _11);
  not not_6 (_12, _13);
endmodule

module _2_input_OR (
  input  _1,
  input  _2,
  input  _4,
  input  _5,
  input  _9,
  input  _10,
  input  _12,
  input  _13,
  output _3,
  output _6,
  output _8,
  output _11
);

  or or_1 (_3, _1, _2);
  or or_2 (_6, _4, _5);
  or or_3 (_8, _9, _10);
  or or_4 (_11, _12, _13);
endmodule

module _3_input_OR (
  input  _14,
  input  _1,
  input  _2,
  input  _8,
  input  _3,
  input  _4,
  input  _5,
  input  _11,
  input  _12,
  input  _13,
  input  _7,
  output _9,
  output _6,
  output _10
);

  wire or_1_out, or_2_out, or_3_out;

  or or_1 (or_1_out, _1, _2);
  or or_2 (or_2_out, _3, _4);
  or or_3 (or_3_out, _11, _12);
  or or_4 (_9, or_1_out, _8);
  or or_5 (_6, or_2_out, _5);
  or or_6 (_10, or_3_out, _13);
endmodule

module _3_input_AND (
  input  _14,
  input  _1,
  input  _2,
  input  _13,
  input  _3,
  input  _4,
  input  _5,
  input  _9,
  input  _10,
  input  _11,
  input  _7,
  output _12,
  output _6,
  output _8
);

  wire and_1_out, and_2_out, and_3_out;

  and and_1 (and_1_out, _1, _2);
  and and_2 (and_2_out, _3, _4);
  and and_3 (and_3_out, _9, _10);
  and and_4 (_12, and_1_out, _13);
  and and_5 (_6, and_2_out, _5);
  and and_6 (_8, and_3_out, _11);
endmodule

module _7483_IC (
  input  C_in,
  input  B4,
  input  B3,
  input  B2,
  input  B1,
  input  A4,
  input  A3,
  input  A2,
  input  A1,
  output C_out,
  output S4,
  output S3,
  output S2,
  output S1
);

  wire and_1_out, and_2_out, and_3_out, and_4_out, and_5_out, and_6_out, and_7_out, and_8_out, or_1_out,
       or_2_out, or_3_out, xor_1_out, xor_2_out, xor_3_out, xor_4_out;

  xor xor_1 (xor_1_out, A1, B1);
  and and_1 (and_1_out, A1, B1);
  xor xor_2 (xor_2_out, A2, B2);
  and and_2 (and_2_out, A2, B2);
  xor xor_3 (xor_3_out, A3, B3);
  and and_3 (and_3_out, A3, B3);
  xor xor_4 (xor_4_out, A4, B4);
  and and_4 (and_4_out, A4, B4);
  and and_5 (and_5_out, xor_1_out, C_in);
  xor xor_5 (S1, xor_1_out, C_in);
  xor xor_6 (S2, xor_2_out, or_1_out);
  and and_6 (and_6_out, xor_2_out, or_1_out);
  xor xor_7 (S3, xor_3_out, or_3_out);
  and and_7 (and_7_out, xor_3_out, or_3_out);
  xor xor_8 (S4, xor_4_out, or_2_out);
  and and_8 (and_8_out, xor_4_out, or_2_out);
  or or_1 (or_1_out, and_5_out, and_1_out);
  or or_2 (or_2_out, and_7_out, and_3_out);
  or or_3 (or_3_out, and_6_out, and_2_out);
  or or_4 (C_out, and_8_out, and_4_out);
endmodule

module XOR_IC (
  input  _1,
  input  _2,
  input  _4,
  input  _5,
  input  _10,
  input  _9,
  input  _13,
  input  _12,
  output _3,
  output _6,
  output _8,
  output _11
);

  xor xor_1 (_3, _1, _2);
  xor xor_2 (_6, _4, _5);
  xor xor_3 (_8, _10, _9);
  xor xor_4 (_11, _13, _12);
endmodule

module _4_1_MUX (
  input  I0,
  input  I1,
  input  I2,
  input  I3,
  input  S1,
  input  S0,
  output out_7
);

  wire and_1_out, and_2_out, and_3_out, and_4_out, not_1_out, not_2_out, or_1_out, or_2_out;

  not not_1 (not_1_out, S0);
  not not_2 (not_2_out, S1);
  and and_1 (and_1_out, I0, not_2_out, not_1_out);
  and and_2 (and_2_out, I1, not_2_out, S0);
  and and_3 (and_3_out, I2, S1, not_1_out);
  and and_4 (and_4_out, I3, S1, S0);
  or or_1 (or_1_out, and_1_out, and_2_out);
  or or_2 (or_2_out, and_3_out, and_4_out);
  or or_3 (out_7, or_1_out, or_2_out);
endmodule

module _8_1_MUX (
  input  _17,
  input  _16,
  input  _15,
  input  _14,
  input  S0,
  input  _13,
  input  _12,
  input  _11,
  input  _10,
  input  S1,
  input  S2,
  output out_12
);

  wire n4_1_mux_1_out_7, n4_1_mux_2_out_7;

  _4_1_MUX u_4_1_mux_1 (.I0(_14), .I1(_15), .I2(_16), .I3(_17), .S1(S2), .S0(S1), .out_7(n4_1_mux_1_out_7));
  _4_1_MUX u_4_1_mux_2 (.I0(_10), .I1(_11), .I2(_12), .I3(_13), .S1(S1), .S0(S2), .out_7(n4_1_mux_2_out_7));
  Multiplexer #(.enable("false")) multiplexer_1 (
    .in0(n4_1_mux_1_out_7), .in1(n4_1_mux_2_out_7), .out(out_12), .sel(S0));
endmodule

module JK_flip_flop_IC (
  input  J,
  input  Preset,
  input  K,
  input  Clear,
  input  Clock,
  output Q,
  output Q_prime
);

  wire and_1_out, and_2_out, and_3_out, and_4_out, nor_1_out, nor_2_out, not_1_out, or_1_out, or_2_out;

  or or_1 (or_1_out, J, Preset);
  or or_2 (or_2_out, Preset, K);
  and and_1 (and_1_out, Q_prime, or_1_out, Clock);
  and and_2 (and_2_out, Clock, or_2_out, Q);
  not not_1 (not_1_out, Clock);
  nor nor_1 (nor_1_out, and_1_out, nor_2_out);
  nor nor_2 (nor_2_out, nor_1_out, and_2_out, Clear);
  and and_3 (and_3_out, not_1_out, nor_1_out);
  nor nor_3 (Q, and_3_out, Q_prime);
  and and_4 (and_4_out, nor_2_out, not_1_out);
  nor nor_4 (Q_prime, Q, and_4_out);
endmodule

module D_flip_flop_IC (
  input  D,
  input  CLOCK,
  input  in_3,
  input  in_4,
  output out_5,
  output out_6
);

  wire not_1_out;

  not not_1 (not_1_out, D);
  JK_flip_flop_IC jk_flip_flop_ic_1 (
    .J(D), .Preset(in_3), .K(not_1_out), .Q(out_5), .Q_prime(out_6), .Clock(CLOCK), .Clear(in_4));
endmodule

module T_flip_flop_IC (
  input  in_1,
  input  in_2,
  input  in_3,
  input  in_4,
  output out_5,
  output out_6
);

  JK_flip_flop_IC jk_flip_flop_ic_1 (
    .J(in_1), .Preset(in_3), .K(in_1), .Q(out_5), .Q_prime(out_6), .Clock(in_2), .Clear(in_4));
endmodule

module \new  (
  input  in_1,
  input  in_2,
  input  [1:0] in_3,
  input  in_4,
  input  in_5,
  input  in_6,
  output out_7,
  output out_8
);

  wire and_1_out, and_2_out, not_1_out, not_2_out, or_1_out, or_2_out, xor_1_out, xor_2_out;

  and and_1 (and_1_out, in_1, in_2);
  or or_1 (or_1_out, in_1, in_2);
  xor xor_1 (xor_1_out, in_1, in_2);
  not not_1 (not_1_out, in_1);
  and and_2 (and_2_out, in_5, in_6);
  or or_2 (or_2_out, in_5, in_6);
  xor xor_2 (xor_2_out, in_5, in_6);
  not not_2 (not_2_out, in_5);
  Multiplexer #(.select(2)) multiplexer_1 (
    .in0(and_1_out), .in1(or_1_out), .in2(xor_1_out), .in3(not_1_out), .out(out_7), .sel(in_3), .en(in_4));
  Multiplexer #(.select(2)) multiplexer_2 (
    .in0(and_2_out), .in1(or_2_out), .in2(xor_2_out), .in3(not_2_out), .out(out_8), .sel(in_3), .en(in_4));
endmodule
