// Logisim project lab6.circ as structural Verilog: 4 circuits, main circuit main
module main (
  input  in_1,
  input  in_2,
  input  [2:0] in_3,
  input  [2:0] in_4,
  input  [2:0] in_5,
  input  [1:0] in_6,
  output [11:0] out_7,
  output out_8,
  output [11:0] out_9,
  output [11:0] out_10
);

  wire clock_1_out;

  Clock clock_1 (.out(clock_1_out));
  _12_bit_register u_12_bit_register_1 (
    .Write_data(out_7), .Read_Data_1(out_9), .Read_Register_1(in_3), .Read_Data_2(out_10),
    .Read_Register_2(in_4), .Write_Register(in_5), .Write_Enable_Key(in_1), .Clock(clock_1_out));
  _12_Bit_ALU u_12_bit_alu_1 (.in_1(in_2), .in_2(out_9), .in_3(out_10), .in_4(in_6), .out_5(out_7), .Cout(out_8));
endmodule

module _12_bit_register (
  input  [2:0] Read_Register_1,
  input  [11:0] Write_data,
  input  [2:0] Write_Register,
  input  [2:0] Read_Register_2,
  input  Write_Enable_Key,
  input  Clock,
  output [11:0] Read_Data_1,
  output [11:0] Read_Data_2
);

  wire and_1_out, decoder_1_out0, decoder_1_out1, decoder_1_out2, decoder_1_out3, decoder_1_out4,
       decoder_1_out5, decoder_1_out6, decoder_1_out7;
  wire [11:0] demultiplexer_1_out0, demultiplexer_1_out1, demultiplexer_1_out2, demultiplexer_1_out3,
       demultiplexer_1_out4, demultiplexer_1_out5, demultiplexer_1_out6, demultiplexer_1_out7, register_1_q,
       register_2_q, register_3_q, register_4_q, register_5_q, register_6_q, register_7_q, register_8_q;

  Demultiplexer #(.select(3), .width(12)) demultiplexer_1 (
    .out0(demultiplexer_1_out0), .out1(demultiplexer_1_out1), .out2(demultiplexer_1_out2),
    .out3(demultiplexer_1_out3), .out4(demultiplexer_1_out4), .out5(demultiplexer_1_out5),
    .out6(demultiplexer_1_out6), .out7(demultiplexer_1_out7), .in(Write_data), .sel(Write_Register));  // open: en
  Decoder #(.select(3)) decoder_1 (
    .out0(decoder_1_out0), .out1(decoder_1_out1), .out2(decoder_1_out2), .out3(decoder_1_out3),
    .out4(decoder_1_out4), .out5(decoder_1_out5), .out6(decoder_1_out6), .out7(decoder_1_out7),
    .sel(Write_Register));  // open: en
  and and_1 (and_1_out, Write_Enable_Key, Clock);
  Register #(.width(12)) register_1 (
    .D(demultiplexer_1_out0), .en(decoder_1_out0), .Q(register_1_q), .clk(and_1_out));  // open: clr
  Register #(.width(12)) register_2 (
    .D(demultiplexer_1_out1), .en(decoder_1_out1), .Q(register_2_q), .clk(and_1_out));  // open: clr
  Register #(.width(12)) register_3 (
    .D(demultiplexer_1_out2), .en(decoder_1_out2), .Q(register_3_q), .clk(and_1_out));  // open: clr
  Register #(.width(12)) register_4 (
    .D(demultiplexer_1_out3), .en(decoder_1_out3), .Q(register_4_q), .clk(and_1_out));  // open: clr
  Register #(.width(12)) register_5 (
    .D(demultiplexer_1_out4), .en(decoder_1_out4), .Q(register_5_q), .clk(and_1_out));  // open: clr
  Register #(.width(12)) register_6 (
    .D(demultiplexer_1_out5), .en(decoder_1_out5), .Q(register_6_q), .clk(and_1_out));  // open: clr
  Register #(.width(12)) register_7 (
    .D(demultiplexer_1_out6), .en(decoder_1_out6), .Q(register_7_q), .clk(and_1_out));  // open: clr
  Register #(.width(12)) register_8 (
    .D(demultiplexer_1_out7), .en(decoder_1_out7), .Q(register_8_q), .clk(and_1_out));  // open: clr
  Multiplexer #(.select(3), .width(12)) multiplexer_1 (
    .in0(register_1_q), .in1(register_2_q), .in2(register_3_q), .in3(register_4_q), .in4(register_5_q),
    .in5(register_6_q), .in6(register_7_q), .in7(register_8_q), .out(Read_Data_1), .sel(Read_Register_1));  // open: en
  Multiplexer #(.select(3), .width(12)) multiplexer_2 (
    .in0(register_1_q), .in1(register_2_q), .in2(register_3_q), .in3(register_4_q), .in4(register_5_q),
    .in5(register_6_q), .in6(register_7_q), .in7(register_8_q), .out(Read_Data_2), .sel(Read_Register_2));  // open: en
endmodule

module _1_Bit_ALU (
  input  Cin,
  input  A,
  input  B,
  input  [1:0] Opcode,
  output Output,
  output Cout
);

  wire adder_1_cout, adder_1_out, and_1_out, or_1_out, subtractor_1_bout, subtractor_1_out;

  and and_1 (and_1_out, A, B);
  or or_1 (or_1_out, A, B);
  Adder #(.width(1)) adder_1 (.a(A), .b(B), .out(adder_1_out), .cin(Cin), .cout(adder_1_cout));
  Subtractor #(.width(1)) subtractor_1 (.a(A), .b(B), .out(subtractor_1_out), .bin(Cin), .bout(subtractor_1_bout));
  Multiplexer multiplexer_1 (.in0(adder_1_cout), .in1(subtractor_1_bout), .out(Cout), .sel(Opcode[0]), .en(Opcode[1]));
  Multiplexer #(.select(2)) multiplexer_2 (
    .in0(and_1_out), .in1(or_1_out), .in2(adder_1_out), .in3(subtractor_1_out), .out(Output), .sel(Opcode));  // open: en
endmodule

module _12_Bit_ALU (
  input  in_1,
  input  [11:0] in_2,
  input  [11:0] in_3,
  input  [1:0] in_4,
  output [11:0] out_5,
  output Cout
);

  wire n1_bit_alu_1_cout, n1_bit_alu_2_cout, n1_bit_alu_3_cout, n1_bit_alu_4_cout, n1_bit_alu_5_cout,
       n1_bit_alu_6_cout, n1_bit_alu_7_cout, n1_bit_alu_8_cout, n1_bit_alu_9_cout, n1_bit_alu_10_cout,
       n1_bit_alu_11_cout;

  _1_Bit_ALU u_1_bit_alu_1 (
    .Cin(in_1), .A(in_2[0]), .B(in_3[0]), .Output(out_5[0]), .Cout(n1_bit_alu_1_cout), .Opcode(in_4));
  _1_Bit_ALU u_1_bit_alu_2 (
    .Cin(n1_bit_alu_1_cout), .A(in_2[1]), .B(in_3[1]), .Output(out_5[1]), .Cout(n1_bit_alu_2_cout),
    .Opcode(in_4));
  _1_Bit_ALU u_1_bit_alu_3 (
    .Cin(n1_bit_alu_2_cout), .A(in_2[2]), .B(in_3[2]), .Output(out_5[2]), .Cout(n1_bit_alu_3_cout),
    .Opcode(in_4));
  _1_Bit_ALU u_1_bit_alu_4 (
    .Cin(n1_bit_alu_3_cout), .A(in_2[3]), .B(in_3[3]), .Output(out_5[3]), .Cout(n1_bit_alu_4_cout),
    .Opcode(in_4));
  _1_Bit_ALU u_1_bit_alu_5 (
    .Cin(n1_bit_alu_4_cout), .A(in_2[4]), .B(in_3[4]), .Output(out_5[4]), .Cout(n1_bit_alu_5_cout),
    .Opcode(in_4));
  _1_Bit_ALU u_1_bit_alu_6 (
    .Cin(n1_bit_alu_5_cout), .A(in_2[5]), .B(in_3[5]), .Output(out_5[5]), .Cout(n1_bit_alu_6_cout),
    .Opcode(in_4));
  _1_Bit_ALU u_1_bit_alu_7 (
    .Cin(n1_bit_alu_6_cout), .A(in_2[6]), .B(in_3[6]), .Output(out_5[6]), .Cout(n1_bit_alu_7_cout),
    .Opcode(in_4));
  _1_Bit_ALU u_1_bit_alu_8 (
    .Cin(n1_bit_alu_7_cout), .A(in_2[7]), .B(in_3[7]), .Output(out_5[7]), .Cout(n1_bit_alu_8_cout),
    .Opcode(in_4));
  _1_Bit_ALU u_1_bit_alu_9 (
    .Cin(n1_bit_alu_8_cout), .A(in_2[8]), .B(in_3[8]), .Output(out_5[8]), .Cout(n1_bit_alu_9_cout),
    .Opcode(in_4));
  _1_Bit_ALU u_1_bit_alu_10 (
    .Cin(n1_bit_alu_9_cout), .A(in_2[9]), .B(in_3[9]), .Output(out_5[9]), .Cout(n1_bit_alu_10_cout),
    .Opcode(in_4));
  _1_Bit_ALU u_1_bit_alu_11 (
    .Cin(n1_bit_alu_10_cout), .A(in_2[10]), .B(in_3[10]), .Output(out_5[10]), .Cout(n1_bit_alu_11_cout),
    .Opcode(in_4));
  _1_Bit_ALU u_1_bit_alu_12 (
    .Cin(n1_bit_alu_11_cout), .A(in_2[11]), .B(in_3[11]), .Output(out_5[11]), .Cout(Cout), .Opcode(in_4));
endmodule
